# Fritzing sketch MQ-9 calibration (saved by Fritzing 0.9.4)
breadboards: 1

parts:
  Part1 = MQ-9 breakout  # not connected
  Part2 = Arduino Uno (Rev3)
  LED1 = LED - 5mm [color="Green (560nm)" package="5 mm [THT]"]

nets:
  N1: Part2.D2, LED1.anode
  N2: Part2.GND, LED1.cathode

custom parts:
  MQ-9 breakout: SKU: 101284
